// Logisim project G05.circ as structural Verilog: 8 circuits, main circuit guia_0501
module guia_0501 (
  input  A,
  input  B,
  input  A_2,
  input  B_2,
  output a_prime___b__prime
);

  wire nor_1_out, nor_2_out, nor_3_out, nor_5_out;

  nor nor_1 (nor_1_out, A, A);
  nor nor_2 (nor_2_out, A_2, A_2);
  nor nor_3 (nor_3_out, B_2, B_2);
  nor nor_4 (a_prime___b__prime, nor_1_out, B);
  nor nor_5 (nor_5_out, nor_3_out, nor_3_out);
  // NOR_Gate nor_6 has open pins: in0=nor_2_out, in1=nor_5_out, out=open

  // Notes on the sheet:
  //   (a & ~b)
  //   b
  //   ~b
  //   ~a
  //   ~a
  //   b
  //   (a'|b)'
endmodule

module guia_0502 (
  input  A,
  input  B,
  input  A_2,
  input  B_2,
  output out_5,
  output out_6
);

  wire nand_1_out, nand_2_out, nand_3_out, nand_5_out;

  nand nand_1 (nand_1_out, A_2, A_2);
  nand nand_2 (nand_2_out, B_2, B_2);
  nand nand_3 (nand_3_out, B, B);
  nand nand_4 (out_5, A, nand_3_out);
  nand nand_5 (nand_5_out, nand_1_out, nand_1_out);
  nand nand_6 (out_6, nand_5_out, nand_2_out);

  // Notes on the sheet:
  //   *usar nand
  //    ( ~a | b )
  //   a
  //   b'
  //   (a & b') ' = a' | b
endmodule

module guia_0503 (
  input  A,
  input  B,
  input  A_2,
  input  B_2,
  output out_5,
  output a_prime___b__prime
);

  wire nor_1_out, nor_2_out, nor_3_out, nor_5_out;

  nor nor_1 (nor_1_out, B, B);
  nor nor_2 (nor_2_out, A_2, A_2);
  nor nor_3 (nor_3_out, B_2, B_2);
  nor nor_4 (out_5, A, nor_1_out);
  nor nor_5 (nor_5_out, nor_2_out, nor_2_out);
  nor nor_6 (a_prime___b__prime, nor_5_out, nor_3_out);

  // Notes on the sheet:
  //   (a | b' )' = a' & b
  //   a'
  //   b'
  //   a
endmodule

module guia_0504 (
  input  A,
  input  B,
  input  A_2,
  input  B_2,
  output out_5,
  output out_6
);

  wire nand_1_out, nand_2_out, nand_3_out, nand_5_out;

  nand nand_1 (nand_1_out, B, B);
  nand nand_2 (nand_2_out, A_2, A_2);
  nand nand_3 (nand_3_out, B_2, B_2);
  nand nand_4 (out_5, A, nand_1_out);
  nand nand_5 (nand_5_out, nand_2_out, nand_2_out);
  nand nand_6 (out_6, nand_5_out, nand_3_out);

  // Notes on the sheet:
  //   ~(a & ~b) = a' | b
  //   a
  //   b'
  //   a'
  //   b'
  //   a
endmodule

module guia_0505 (
  input  A,
  input  B,
  output out_3
);

  wire nor_1_out, nor_2_out, nor_3_out, nor_4_out, nor_5_out, nor_6_out, nor_7_out;

  nor nor_1 (nor_1_out, A, A);
  nor nor_2 (nor_2_out, B, B);
  nor nor_3 (nor_3_out, nor_1_out, nor_1_out);
  nor nor_4 (nor_4_out, nor_2_out, nor_2_out);
  nor nor_5 (nor_5_out, nor_3_out, nor_2_out);
  nor nor_6 (nor_6_out, nor_1_out, nor_4_out);
  nor nor_7 (nor_7_out, nor_5_out, nor_6_out);
  nor nor_8 (out_3, nor_7_out, nor_7_out);

  // Notes on the sheet:
  //   ((a ^ b) = a xor b)
  //   a'
  //   b'
  //   a
  //   b
  //   a'&b
  //   a&b'
endmodule

module guia_0506 (
  input  A,
  input  B,
  output out_3
);

  wire nand_1_out, nand_2_out, nand_3_out, nand_4_out;

  nand nand_1 (nand_1_out, B, B);
  nand nand_2 (nand_2_out, A, A);
  nand nand_3 (nand_3_out, A, B);
  nand nand_4 (nand_4_out, nand_2_out, nand_1_out);
  nand nand_5 (out_3, nand_4_out, nand_3_out);

  // Notes on the sheet:
  //   (~(a & b) = a xnor b)
  //   a'
  //     a' & b'
  //   b'
  //   a & b
  //   (a & b)' + (a & b)
endmodule

module guia_0507 (
  input  A,
  input  B,
  output a___b
);

  wire nor_1_out;

  nor nor_1 (nor_1_out, A, B);
  nor nor_2 (a___b, nor_1_out, nor_1_out);

  // Notes on the sheet:
  //   (a'  & b')' = a + b
  //   a' & b'
endmodule

module guia_0508 (
  input  A,
  input  B,
  output out_3
);

  wire nand_1_out, nand_2_out;

  nand nand_1 (nand_1_out, A, A);
  nand nand_2 (nand_2_out, B, B);
  nand nand_3 (out_3, nand_1_out, nand_2_out);

  // Notes on the sheet:
  //   (a' | b')
  //   a'
  //   b'
  //   (a&b)
endmodule
