// Logisim project guia06 (1).circ as structural Verilog: 5 circuits, main circuit guia0602a
module guia0602a (
  input  x,
  input  y,
  input  z,
  output out_4
);

  wire not_1_out, not_2_out, not_3_out, or_1_out, or_2_out;

  not not_1 (not_1_out, x);
  not not_2 (not_2_out, z);
  not not_3 (not_3_out, z);
  or or_1 (or_1_out, not_1_out, not_2_out);
  or or_2 (or_2_out, y, not_3_out);
  and and_1 (out_4, or_1_out, or_2_out);
endmodule

module guia0602b (
  input  x,
  input  y,
  input  z,
  output out_4
);

  wire not_1_out, or_1_out, or_2_out;

  not not_1 (not_1_out, x);
  or or_1 (or_1_out, not_1_out, z);
  or or_2 (or_2_out, y, z);
  and and_1 (out_4, or_1_out, or_2_out);
endmodule

module guia0602c (
  input  x,
  input  y,
  input  z,
  output out_4
);

  wire not_1_out, not_2_out, or_1_out, or_2_out;

  not not_1 (not_1_out, z);
  not not_2 (not_2_out, y);
  or or_1 (or_1_out, x, not_1_out);
  or or_2 (or_2_out, not_2_out, z);
  and and_1 (out_4, or_1_out, or_2_out);
endmodule

module guia0602d (
  input  x,
  input  y,
  input  z,
  output out_4
);

  wire not_1_out, not_2_out, not_3_out, or_1_out, or_2_out, or_3_out;

  not not_1 (not_1_out, z);
  not not_2 (not_2_out, x);
  not not_3 (not_3_out, y);
  or or_1 (or_1_out, x, y);
  or or_2 (or_2_out, y, not_1_out);
  or or_3 (or_3_out, not_2_out, not_3_out, z);
  and and_1 (out_4, or_1_out, or_2_out, or_3_out);
endmodule

module guia0602e (
  input  x,
  input  y,
  input  in_3,
  output out_4
);

  wire not_1_out, not_2_out, not_3_out, or_1_out, or_2_out, or_3_out;

  not not_1 (not_1_out, x);
  not not_2 (not_2_out, y);
  not not_3 (not_3_out, in_3);
  or or_1 (or_1_out, y, in_3);
  or or_2 (or_2_out, x, in_3);
  or or_3 (or_3_out, not_1_out, not_2_out, not_3_out);
  and and_1 (out_4, or_1_out, or_2_out, or_3_out);
endmodule
