// Logisim project guia06 (2).circ as structural Verilog: 5 circuits, main circuit guia0603a
module guia0603a (
  input  x,
  input  y,
  input  w,
  input  z,
  output out_5
);

  wire and_1_out, and_2_out, and_3_out, and_4_out, not_1_out, not_2_out, not_3_out, not_4_out, not_5_out,
       not_6_out, not_7_out, not_8_out;

  not not_1 (not_1_out, x);
  not not_2 (not_2_out, z);
  not not_3 (not_3_out, w);
  not not_4 (not_4_out, z);
  not not_5 (not_5_out, z);
  not not_6 (not_6_out, x);
  not not_7 (not_7_out, y);
  not not_8 (not_8_out, w);
  and and_1 (and_1_out, not_1_out, w, not_2_out);
  and and_2 (and_2_out, x, not_3_out, not_4_out);
  and and_3 (and_3_out, x, y, not_5_out);
  and and_4 (and_4_out, not_6_out, not_7_out, not_8_out, z);
  or or_1 (out_5, and_1_out, and_2_out, and_3_out, and_4_out);
endmodule

module guia0603b (
  input  x,
  input  y,
  input  w,
  input  z,
  output out_5
);

  wire and_1_out, and_2_out, and_3_out, and_4_out, not_1_out, not_2_out, not_3_out, not_4_out, not_5_out,
       not_6_out, not_7_out;

  not not_1 (not_1_out, y);
  not not_2 (not_2_out, w);
  not not_3 (not_3_out, z);
  not not_4 (not_4_out, w);
  not not_5 (not_5_out, z);
  not not_6 (not_6_out, x);
  not not_7 (not_7_out, y);
  and and_1 (and_1_out, not_1_out, not_2_out, not_3_out);
  and and_2 (and_2_out, x, not_4_out, not_5_out);
  and and_3 (and_3_out, not_6_out, not_7_out, z);
  and and_4 (and_4_out, y, w, z);
  or or_1 (out_5, and_1_out, and_2_out, and_3_out, and_4_out);
endmodule

module guia0603c (
  input  x,
  input  y,
  input  w,
  input  z,
  output out_5
);

  wire and_1_out, and_2_out, and_3_out, and_4_out, not_1_out, not_2_out, not_3_out, not_4_out, not_5_out;

  not not_1 (not_1_out, x);
  not not_2 (not_2_out, y);
  not not_3 (not_3_out, w);
  and and_1 (and_1_out, y, w, z);
  not not_4 (not_4_out, y);
  not not_5 (not_5_out, z);
  and and_2 (and_2_out, x, w);
  and and_3 (and_3_out, not_1_out, not_2_out, not_3_out);
  and and_4 (and_4_out, not_4_out, w, not_5_out);
  or or_1 (out_5, and_2_out, and_3_out, and_1_out, and_4_out);
endmodule

module guia0603d (
  input  x,
  input  y,
  input  w,
  input  z,
  output out_5
);

  wire and_1_out, and_2_out, and_3_out, not_1_out, not_2_out, not_3_out, not_4_out;

  not not_1 (not_1_out, z);
  not not_2 (not_2_out, w);
  not not_3 (not_3_out, x);
  not not_4 (not_4_out, z);
  and and_1 (and_1_out, w, not_1_out);
  and and_2 (and_2_out, y, not_2_out, z);
  and and_3 (and_3_out, not_3_out, y, not_4_out);
  or or_1 (out_5, and_1_out, and_2_out, and_3_out);
endmodule

module guia0603e (
  input  x,
  input  y,
  input  w,
  input  z,
  output out_5
);

  wire and_1_out, and_2_out, and_3_out, not_1_out, not_2_out, not_3_out, not_4_out;

  not not_1 (not_1_out, y);
  not not_2 (not_2_out, w);
  not not_3 (not_3_out, y);
  not not_4 (not_4_out, w);
  and and_1 (and_1_out, not_1_out, not_2_out);
  and and_2 (and_2_out, not_3_out, z);
  and and_3 (and_3_out, not_4_out, z);
  or or_1 (out_5, and_1_out, and_2_out, and_3_out);
endmodule
