// Logisim project guia06 (3).circ as structural Verilog: 5 circuits, main circuit guia0604a
module guia0604a (
  input  x,
  input  y,
  input  w,
  input  z,
  output out_5
);

  wire not_1_out, not_2_out, not_3_out, not_4_out, not_5_out, or_1_out, or_2_out, or_3_out;

  not not_1 (not_1_out, y);
  not not_2 (not_2_out, z);
  not not_3 (not_3_out, y);
  not not_4 (not_4_out, z);
  not not_5 (not_5_out, w);
  or or_1 (or_1_out, not_1_out, w, not_2_out);
  or or_2 (or_2_out, x, not_3_out, not_4_out);
  or or_3 (or_3_out, x, y, not_5_out, z);
  and and_1 (out_5, or_1_out, or_2_out, or_3_out);
endmodule

module guia0604b (
  input  x,
  input  y,
  input  w,
  input  z,
  output out_5
);

  wire not_1_out, not_2_out, not_3_out, not_4_out, not_5_out, or_1_out, or_2_out, or_3_out;

  not not_1 (not_1_out, x);
  not not_2 (not_2_out, z);
  not not_3 (not_3_out, y);
  not not_4 (not_4_out, w);
  not not_5 (not_5_out, y);
  or or_1 (or_1_out, not_1_out, y, not_2_out);
  or or_2 (or_2_out, not_3_out, not_4_out, z);
  or or_3 (or_3_out, x, not_5_out, z);
  and and_1 (out_5, or_1_out, or_2_out, or_3_out);
endmodule

module guia0604c (
  input  x,
  input  y,
  input  w,
  input  z,
  output out_5
);

  wire not_1_out, not_2_out, not_3_out, not_4_out, not_5_out, or_1_out, or_2_out, or_3_out;

  not not_1 (not_1_out, y);
  not not_2 (not_2_out, x);
  not not_3 (not_3_out, y);
  not not_4 (not_4_out, w);
  not not_5 (not_5_out, z);
  or or_1 (or_1_out, not_1_out, w, z);
  or or_2 (or_2_out, not_2_out, y, z);
  or or_3 (or_3_out, x, not_3_out, not_4_out, not_5_out);
  and and_1 (out_5, or_1_out, or_2_out, or_3_out);
endmodule

module guia0604d (
  input  x,
  input  y,
  input  w,
  input  z,
  output out_5
);

  wire not_1_out, not_2_out, not_3_out, or_1_out, or_2_out;

  not not_1 (not_1_out, z);
  not not_2 (not_2_out, x);
  not not_3 (not_3_out, z);
  or or_1 (or_1_out, w, not_1_out);
  or or_2 (or_2_out, not_2_out, not_3_out);
  and and_1 (out_5, or_1_out, or_2_out);
endmodule

module guia0604e (
  input  x,
  input  y,
  input  w,
  input  z,
  output out_5
);

  wire not_1_out, not_2_out, not_3_out, not_4_out, not_5_out, not_6_out, not_7_out, not_8_out, or_1_out,
       or_2_out, or_3_out, or_4_out;

  not not_1 (not_1_out, w);
  not not_2 (not_2_out, w);
  not not_3 (not_3_out, z);
  not not_4 (not_4_out, y);
  not not_5 (not_5_out, w);
  not not_6 (not_6_out, x);
  not not_7 (not_7_out, y);
  not not_8 (not_8_out, z);
  or or_1 (or_1_out, x, not_1_out);
  or or_2 (or_2_out, y, not_2_out, not_3_out);
  or or_3 (or_3_out, not_4_out, not_5_out, z);
  or or_4 (or_4_out, not_6_out, not_7_out, w, not_8_out);
  and and_1 (out_5, or_1_out, or_2_out, or_3_out, or_4_out);
endmodule
