// Logisim project guia06 (4).circ as structural Verilog: 1 circuit, main circuit main
module main (
  input  x,
  input  y,
  input  z,
  input  x_2,
  input  y_2,
  input  z_2,
  output out_7,
  output out_8
);

  wire and_1_out, and_2_out, and_3_out, and_4_out, and_5_out, not_1_out, not_2_out, not_3_out, not_4_out,
       not_5_out, not_6_out, not_7_out, not_8_out, or_2_out, or_3_out;

  not not_1 (not_1_out, y);
  not not_2 (not_2_out, z);
  and and_1 (and_1_out, x, not_1_out);
  and and_2 (and_2_out, x, not_2_out);
  or or_1 (out_7, and_1_out, and_2_out);
  not not_3 (not_3_out, y_2);
  or or_2 (or_2_out, not_3_out, not_4_out);
  not not_4 (not_4_out, x_2);
  and and_3 (and_3_out, y_2, x_2);
  and and_4 (and_4_out, z_2, y_2);
  not not_5 (not_5_out, x_2);
  not not_6 (not_6_out, or_2_out);
  not not_7 (not_7_out, and_3_out);
  or or_3 (or_3_out, and_4_out, not_5_out);
  not not_8 (not_8_out, or_3_out);
  and and_5 (and_5_out, not_6_out, not_7_out);
  or or_4 (out_8, and_5_out, not_8_out);

  // Notes on the sheet:
  //   versão completa
  //   versão simplificada
endmodule
