// Logisim project guia06 (6).circ as structural Verilog: 5 circuits, main circuit guia0601a
module guia0601a (
  input  X,
  input  Y,
  input  Z,
  output out_4
);

  wire and_1_out, and_2_out, not_1_out;

  not not_1 (not_1_out, Y);
  and and_1 (and_1_out, X, Z);
  and and_2 (and_2_out, not_1_out, Z);
  or or_1 (out_4, and_1_out, and_2_out);
endmodule

module guia0601b (
  input  x,
  input  y,
  input  z,
  output out_4
);

  wire and_1_out, and_2_out, not_1_out, not_2_out, not_3_out;

  not not_1 (not_1_out, y);
  not not_2 (not_2_out, z);
  not not_3 (not_3_out, z);
  and and_1 (and_1_out, not_1_out, not_2_out);
  and and_2 (and_2_out, x, not_3_out);
  or or_1 (out_4, and_1_out, and_2_out);
endmodule

module guia0601c (
  input  x,
  input  y,
  input  z,
  output out_4
);

  wire and_1_out, and_2_out, not_1_out, not_2_out;

  not not_1 (not_1_out, x);
  not not_2 (not_2_out, z);
  and and_1 (and_1_out, not_1_out, z);
  and and_2 (and_2_out, y, not_2_out);
  or or_1 (out_4, and_1_out, and_2_out);
endmodule

module guia0601e (
  input  x,
  input  y,
  input  z,
  output out_4
);

  wire and_1_out, and_2_out, and_3_out, not_1_out, not_2_out, not_3_out, not_4_out;

  not not_1 (not_1_out, x);
  not not_2 (not_2_out, z);
  not not_3 (not_3_out, y);
  not not_4 (not_4_out, z);
  and and_1 (and_1_out, not_1_out, not_2_out);
  and and_2 (and_2_out, not_3_out, not_4_out);
  and and_3 (and_3_out, x, y, z);
  or or_1 (out_4, and_1_out, and_2_out, and_3_out);
endmodule

module guia0601d (
  input  x,
  input  y,
  input  z,
  output out_4
);

  wire and_1_out, and_2_out, not_1_out, not_2_out;

  not not_1 (not_1_out, z);
  not not_2 (not_2_out, y);
  and and_1 (and_1_out, y, not_1_out);
  and and_2 (and_2_out, not_2_out, z);
  or or_1 (out_4, and_1_out, and_2_out);
endmodule
