// Logisim project G701-Log.circ as structural Verilog: 1 circuit, main circuit main
module main (
  input  a,
  input  b,
  input  in_3,
  output out_4,
  output out_5
);

  wire nand_1_out;

  and and_1 (out_4, a, in_3);
  and and_2 (out_5, b, nand_1_out);
  nand nand_1 (nand_1_out, in_3, in_3);

  // Notes on the sheet:
  //   1 == a; 0 == b;
  //   Rafael Sampaio - 866307
endmodule
