// Logisim project G702-Log.circ as structural Verilog: 1 circuit, main circuit main
module main (
  input  a,
  input  b,
  input  in_3,
  output out_4
);

  wire nor_1_out, nor_2_out, nor_3_out, nor_4_out, nor_5_out;

  nor nor_1 (nor_1_out, a, a);
  nor nor_2 (nor_2_out, b, b);
  nor nor_3 (nor_3_out, in_3, in_3);
  nor nor_4 (nor_4_out, nor_1_out, in_3);
  nor nor_5 (nor_5_out, nor_2_out, nor_3_out);
  or or_1 (out_4, nor_4_out, nor_5_out);

  // Notes on the sheet:
  //   Rafael Sampaio - 866307
  //   0 == a; 1 == b;
endmodule
