// Logisim project G703-Log.circ as structural Verilog: 1 circuit, main circuit main
module main (
  input  a,
  input  b,
  input  in_3,
  input  a_2,
  input  in_5,
  input  b_2,
  input  in_7,
  output out_8
);

  wire and_1_out, and_2_out, nand_1_out, nand_2_out, nand_3_out, nand_4_out, nor_1_out, nor_2_out, nor_3_out,
       nor_4_out, nor_5_out, nor_6_out, nor_7_out, nor_8_out, nor_9_out, nor_10_out, or_1_out;

  nor nor_1 (nor_1_out, a, a);
  nor nor_2 (nor_2_out, b, b);
  nand nand_1 (nand_1_out, in_7, in_7);
  nor nor_3 (nor_3_out, nor_1_out, in_3);
  nor nor_4 (nor_4_out, nor_2_out, nor_5_out);
  nor nor_5 (nor_5_out, in_3, in_3);
  and and_1 (and_1_out, a_2, in_7);
  and and_2 (and_2_out, b_2, nand_1_out);
  or or_1 (or_1_out, nor_3_out, nor_4_out);
  nand nand_2 (nand_2_out, and_1_out, and_1_out);
  nand nand_3 (nand_3_out, nand_2_out, nand_4_out);
  nand nand_4 (nand_4_out, and_2_out, and_2_out);
  nor nor_6 (nor_6_out, or_1_out, or_1_out);
  nor nor_7 (nor_7_out, nand_3_out, nand_3_out);
  nor nor_8 (nor_8_out, nor_6_out, in_5);
  nor nor_9 (nor_9_out, nor_7_out, nor_10_out);
  nor nor_10 (nor_10_out, in_5, in_5);
  or or_2 (out_8, nor_8_out, nor_9_out);

  // Notes on the sheet:
  //   Rafael Sampaio - 866307
endmodule
