// Logisim project G704-Log.circ as structural Verilog: 1 circuit, main circuit main
module main (
  input  a,
  input  b,
  input  a_2,
  input  b_2,
  input  in_5,
  input  in_6,
  output out_7
);

  wire and_1_out, and_2_out, nor_1_out, nor_2_out, nor_3_out, nor_4_out, nor_5_out, nor_6_out, nor_7_out,
       nor_8_out, nor_9_out, nor_10_out, or_1_out, xnor_1_out, xor_1_out, xor_2_out;

  nor nor_1 (nor_1_out, a, a);
  nor nor_2 (nor_2_out, b, b);
  xnor xnor_1 (xnor_1_out, in_5, in_5);
  nor nor_3 (nor_3_out, nor_1_out, in_5);
  nor nor_4 (nor_4_out, nor_2_out, nor_5_out);
  nor nor_5 (nor_5_out, in_5, in_5);
  and and_1 (and_1_out, a_2, in_5);
  and and_2 (and_2_out, b_2, xor_1_out);
  xor xor_1 (xor_1_out, xnor_1_out, in_5);
  or or_1 (or_1_out, nor_3_out, nor_4_out);
  xor xor_2 (xor_2_out, and_1_out, and_2_out);
  nor nor_6 (nor_6_out, or_1_out, or_1_out);
  nor nor_7 (nor_7_out, xor_2_out, xor_2_out);
  nor nor_8 (nor_8_out, in_6, in_6);
  nor nor_9 (nor_9_out, nor_6_out, in_6);
  nor nor_10 (nor_10_out, nor_7_out, nor_8_out);
  or or_2 (out_7, nor_9_out, nor_10_out);

  // Notes on the sheet:
  //   Rafael Sampaio - 866307
endmodule
