// Logisim project G705-Log.circ as structural Verilog: 1 circuit, main circuit main
module main (
  input  a,
  input  b,
  input  c,
  input  d,
  input  e,
  input  f,
  input  g,
  input  h,
  input  in_9,
  input  in_10,
  input  in_11,
  output out_12
);

  wire and_1_out, and_2_out, and_3_out, and_4_out, nand_1_out, nand_2_out, nor_1_out, nor_2_out, nor_3_out,
       nor_4_out, nor_5_out, nor_6_out, nor_7_out, nor_8_out, nor_9_out, nor_10_out, nor_11_out, nor_12_out,
       nor_13_out, nor_14_out, nor_15_out, nor_16_out, nor_17_out, nor_18_out, nor_19_out, nor_20_out,
       not_1_out, not_2_out, not_3_out, or_1_out, or_2_out, or_3_out, or_4_out, xnor_1_out, xnor_2_out,
       xor_1_out, xor_2_out, xor_3_out, xor_4_out;

  not not_1 (not_1_out, a);
  nand nand_1 (nand_1_out, b, b);
  xnor xnor_1 (xnor_1_out, in_9, in_9);
  nor nor_1 (nor_1_out, e, e);
  nor nor_2 (nor_2_out, f, f);
  xnor xnor_2 (xnor_2_out, in_9, in_9);
  nor nor_3 (nor_3_out, not_1_out, in_9);
  nor nor_4 (nor_4_out, nand_1_out, nand_2_out);
  nand nand_2 (nand_2_out, in_9, in_9);
  and and_1 (and_1_out, c, in_9);
  and and_2 (and_2_out, d, xor_1_out);
  xor xor_1 (xor_1_out, xnor_1_out, in_9);
  nor nor_5 (nor_5_out, nor_1_out, in_9);
  nor nor_6 (nor_6_out, nor_2_out, nor_7_out);
  nor nor_7 (nor_7_out, in_9, in_9);
  and and_3 (and_3_out, g, in_9);
  and and_4 (and_4_out, h, xor_2_out);
  xor xor_2 (xor_2_out, xnor_2_out, in_9);
  or or_1 (or_1_out, nor_3_out, nor_4_out);
  xor xor_3 (xor_3_out, and_1_out, and_2_out);
  or or_2 (or_2_out, nor_5_out, nor_6_out);
  xor xor_4 (xor_4_out, and_3_out, and_4_out);
  nor nor_8 (nor_8_out, or_1_out, or_1_out);
  nor nor_9 (nor_9_out, xor_3_out, xor_3_out);
  nor nor_10 (nor_10_out, or_2_out, or_2_out);
  nor nor_11 (nor_11_out, xor_4_out, xor_4_out);
  nor nor_12 (nor_12_out, in_10, in_10);
  nor nor_13 (nor_13_out, in_10, in_10);
  nor nor_14 (nor_14_out, nor_8_out, in_10);
  nor nor_15 (nor_15_out, nor_9_out, nor_12_out);
  nor nor_16 (nor_16_out, nor_10_out, in_10);
  nor nor_17 (nor_17_out, nor_11_out, nor_13_out);
  or or_3 (or_3_out, nor_14_out, nor_15_out);
  not not_2 (not_2_out, or_3_out);
  not not_3 (not_3_out, or_4_out);
  or or_4 (or_4_out, nor_16_out, nor_17_out);
  nor nor_18 (nor_18_out, in_11, in_11);
  nor nor_19 (nor_19_out, not_2_out, in_11);
  nor nor_20 (nor_20_out, not_3_out, nor_18_out);
  or or_5 (out_12, nor_19_out, nor_20_out);

  // Notes on the sheet:
  //   Rafael Sampaio - 866307
endmodule
