// Logisim project logisimR01.circ as structural Verilog: 7 circuits, main circuit 1d
module _1d (
  input  a,
  input  b,
  input  in_3,
  input  d,
  output out_5
);

  wire nand_1_out, nand_2_out, nand_3_out, nand_4_out, nand_5_out, nand_6_out, nand_7_out;

  nand nand_1 (nand_1_out, a, a);
  nand nand_2 (nand_2_out, b, d);
  nand nand_3 (nand_3_out, in_3, in_3);
  nand nand_4 (nand_4_out, b, b);
  nand nand_5 (nand_5_out, nand_1_out, d);
  nand nand_6 (nand_6_out, nand_1_out, b, nand_3_out);
  nand nand_7 (nand_7_out, a, in_3, nand_4_out);
  nand nand_8 (out_5, nand_5_out, nand_2_out, nand_6_out, nand_7_out);

  // Notes on the sheet:
  //   a'
  //   a + b'
  //   a+b'+c
  //   a'+b+c'
endmodule

module _1e (
  input  A,
  input  B,
  input  C,
  input  D,
  output out_5
);

  wire nor_1_out, nor_2_out, nor_3_out, nor_4_out, nor_5_out, nor_6_out, nor_7_out;

  nor nor_1 (nor_1_out, C, C);
  nor nor_2 (nor_2_out, A, A);
  nor nor_3 (nor_3_out, B, B);
  nor nor_4 (nor_4_out, B, C, D);
  nor nor_5 (nor_5_out, A, nor_1_out, D);
  nor nor_6 (nor_6_out, nor_2_out, B, C);
  nor nor_7 (nor_7_out, nor_2_out, nor_3_out, D);
  nor nor_8 (out_5, nor_4_out, nor_5_out, nor_6_out, nor_7_out);

  // Notes on the sheet:
  //   A.D'
endmodule

module _2a (
  input  a,
  input  b,
  output out_3
);

  wire not_1_out;

  not not_1 (not_1_out, b);
  Multiplexer multiplexer_1 (.in0(not_1_out), .in1(b), .out(out_3), .sel(a));  // open: en
endmodule

module _2b (
  input  a,
  input  b,
  input  c,
  output out_4
);

  wire nand_1_out, nand_2_out, nand_3_out, nand_4_out;

  nand nand_1 (nand_1_out, a, a);
  nand nand_2 (nand_2_out, b, b);
  nand nand_3 (nand_3_out, nand_1_out, b);
  nand nand_4 (nand_4_out, nand_2_out, c);
  nand nand_5 (out_4, nand_3_out, nand_4_out);
endmodule

module _3a (
  input  a,
  input  b,
  input  c,
  input  d,
  output out_5
);

  wire and_1_out, and_2_out, not_1_out, not_2_out;

  not not_1 (not_1_out, a);
  not not_2 (not_2_out, b);
  and and_1 (and_1_out, not_1_out, d);
  and and_2 (and_2_out, a, not_2_out);
  or or_1 (out_5, and_1_out, and_2_out);
endmodule

module _3b (
  input  a,
  input  b,
  input  c,
  input  d,
  output out_5
);

  wire and_1_out, and_2_out, and_3_out, not_1_out, not_2_out, not_3_out, not_4_out;

  not not_1 (not_1_out, a);
  not not_2 (not_2_out, c);
  not not_3 (not_3_out, b);
  not not_4 (not_4_out, b);
  and and_1 (and_1_out, not_1_out, not_2_out, d);
  and and_2 (and_2_out, a, not_3_out);
  and and_3 (and_3_out, not_4_out, d);
  or or_1 (out_5, and_1_out, and_2_out, and_3_out);
endmodule

module _4a (
  input  a,
  input  b,
  input  c,
  output out_4
);

  wire nand_1_out, nand_2_out, nand_3_out;

  nand nand_1 (nand_1_out, b, b);
  nand nand_2 (nand_2_out, c, c);
  nand nand_3 (nand_3_out, nand_1_out, nand_2_out);
  nand nand_4 (out_4, a, nand_3_out);
endmodule
